// Logisim project se7.1.circ as structural Verilog: 1 circuit, main circuit main
module main (
);

  wire A_p1, A_p2, A_p3, A_p4, and_1_out, and_2_out, and_3_out, and_4_out, and_5_out, and_6_out, and_7_out,
       and_8_out, and_9_out, and_10_out, and_11_out, and_12_out, and_13_out, and_14_out, and_15_out,
       and_16_out, and_17_out, and_18_out, and_19_out, and_20_out, and_21_out, and_22_out, and_23_out,
       and_24_out, and_25_out, and_26_out, and_27_out, and_28_out, and_29_out, and_30_out, and_31_out,
       and_32_out, and_33_out, and_34_out, not_1_out, not_2_out, not_3_out, not_4_out, or_1_out, or_2_out,
       or_3_out, or_4_out, or_5_out, or_6_out, or_7_out;

  // DipSwitch #(.number(4)) A: pin names not known; wires that end beside it: A_p1, A_p2, A_p3, A_p4
  not not_1 (not_1_out, A_p1);
  not not_2 (not_2_out, A_p2);
  not not_3 (not_3_out, A_p3);
  not not_4 (not_4_out, A_p4);
  and and_1 (and_1_out, not_3_out, not_4_out);
  and and_2 (and_2_out, A_p1, not_2_out);
  and and_3 (and_3_out, not_1_out, A_p2, A_p4);
  and and_4 (and_4_out, not_2_out, not_3_out);
  and and_5 (and_5_out, not_2_out, not_4_out);
  and and_6 (and_6_out, not_1_out, not_3_out, not_4_out);
  and and_7 (and_7_out, not_1_out, A_p3, A_p4);
  and and_8 (and_8_out, A_p1, not_3_out, A_p4);
  and and_9 (and_9_out, A_p1, not_2_out, not_4_out);
  and and_10 (and_10_out, A_p1, A_p3, not_4_out);
  and and_11 (and_11_out, not_2_out, not_3_out);
  and and_12 (and_12_out, not_2_out, A_p4);
  and and_13 (and_13_out, not_3_out, A_p4);
  and and_14 (and_14_out, not_1_out, A_p2);
  and and_15 (and_15_out, A_p1, not_2_out);
  and and_16 (and_16_out, not_2_out, not_3_out, not_4_out);
  and and_17 (and_17_out, not_1_out, A_p3, not_4_out);
  and and_18 (and_18_out, not_2_out, A_p3, A_p4);
  and and_19 (and_19_out, A_p2, not_3_out, A_p4);
  and and_20 (and_20_out, not_4_out, A_p1, A_p2);
  and and_21 (and_21_out, not_2_out, not_4_out);
  and and_22 (and_22_out, not_4_out, A_p3);
  and and_23 (and_23_out, A_p1, A_p3);
  and and_24 (and_24_out, A_p1, A_p2);
  and and_25 (and_25_out, A_p1, A_p4);
  and and_26 (and_26_out, A_p1, A_p3);
  and and_27 (and_27_out, not_2_out, not_3_out, not_4_out);
  and and_28 (and_28_out, not_1_out, A_p2, not_4_out);
  and and_29 (and_29_out, A_p2, not_3_out, A_p4);
  and and_30 (and_30_out, not_2_out, A_p3);
  and and_31 (and_31_out, not_4_out, A_p3);
  and and_32 (and_32_out, not_2_out, A_p1);
  and and_33 (and_33_out, A_p1, A_p4);
  and and_34 (and_34_out, not_1_out, A_p2, not_3_out);
  or or_1 (or_1_out, A_p3, and_1_out, and_2_out, and_3_out);
  or or_2 (or_2_out, and_4_out, and_5_out, and_6_out, and_10_out, and_7_out, and_8_out, and_9_out);
  or or_3 (or_3_out, and_11_out, and_12_out, and_13_out, and_14_out, and_15_out);
  or or_4 (or_4_out, and_21_out, and_22_out, and_23_out, and_24_out);
  or or_5 (or_5_out, and_25_out, and_26_out, and_27_out, and_28_out, and_29_out);
  or or_6 (or_6_out, and_30_out, and_31_out, and_32_out, and_33_out, and_34_out);
  or or_7 (or_7_out, and_17_out, and_18_out, and_16_out, and_19_out, and_20_out);
  _7_Segment_Display u_7_segment_display_1 (
    .g(or_6_out), .f(or_5_out), .a(or_1_out), .b(or_2_out), .e(or_4_out), .d(or_7_out), .c(or_3_out));  // open: dp
endmodule
